// Logisim project CPU.circ as structural Verilog
module _1_bit_m (
  input  i,
  input  s,
  output o
);

  wire _1_out, _2_out, _4_out;

  nand _1 (_1_out, i, s);
  nand _2 (_2_out, _1_out, s);
  nand _3 (o, _1_out, _4_out);
  nand _4 (_4_out, o, _2_out);
endmodule

module _8_bit_Register (
  input  i,
  input  i_2,
  input  i_3,
  input  i_4,
  input  i_5,
  input  i_6,
  input  i_7,
  input  i_8,
  input  s,
  input  e,
  output o,
  output o_2,
  output o_3,
  output o_4,
  output o_5,
  output o_6,
  output o_7,
  output o_8
);

  wire n8_bit_memory_1_o, n8_bit_memory_1_o_2, n8_bit_memory_1_o_3, n8_bit_memory_1_o_4, n8_bit_memory_1_o_5,
       n8_bit_memory_1_o_6, n8_bit_memory_1_o_7, n8_bit_memory_1_o_8;

  _8_bit_Memory u_8_bit_memory_1 (
    .o(n8_bit_memory_1_o), .o_2(n8_bit_memory_1_o_2), .o_3(n8_bit_memory_1_o_3), .o_4(n8_bit_memory_1_o_4),
    .o_5(n8_bit_memory_1_o_5), .o_6(n8_bit_memory_1_o_6), .o_7(n8_bit_memory_1_o_7),
    .o_8(n8_bit_memory_1_o_8), .i_2(i_2), .i_3(i_3), .i_4(i_4), .i_5(i_5), .i_6(i_6), .i_7(i_7), .i_8(i_8),
    .s(s), .i(i));
  _8_bit_Enabler u_8_bit_enabler_1 (
    .o_3(o_3), .o_4(o_4), .o_5(o_5), .o_6(o_6), .o_7(o_7), .o_8(o_8), .o(o), .o_2(o_2),
    .i_3(n8_bit_memory_1_o_3), .i_4(n8_bit_memory_1_o_4), .i_5(n8_bit_memory_1_o_5),
    .i_6(n8_bit_memory_1_o_6), .i_7(n8_bit_memory_1_o_7), .i(n8_bit_memory_1_o), .i_8(n8_bit_memory_1_o_8),
    .e(e), .i_2(n8_bit_memory_1_o_2));
endmodule

module _1_byte_Register (
  input  [7:0] i,
  input  s,
  input  e,
  output [7:0] o
);

  wire [7:0] n1_byte_memory_1_o;

  _1_byte_Memory u_1_byte_memory_1 (.o(n1_byte_memory_1_o), .i(i), .s(s));
  _1_byte_Enabler u_1_byte_enabler_1 (.o(o), .i(n1_byte_memory_1_o), .e(e));
endmodule

module test_Register (
  input  in_1,
  input  in_2,
  input  in_3,
  input  in_4,
  input  [7:0] in_5,
  output [7:0] out_6,
  output [7:0] out_7
);

  wire and_1_out, not_1_out, not_2_out;
  wire [7:0] controlled_buffer_1_out;

  not not_1 (not_1_out, in_4);
  not not_2 (not_2_out, in_3);
  and and_1 (and_1_out, not_1_out, not_2_out);
  assign controlled_buffer_1_out = and_1_out ? in_5 : 8'bz;  // Controlled_Buffer controlled_buffer_1
  _1_byte_Register u_1_byte_register_1 (.o(out_6), .s(in_1), .e(in_3), .i(controlled_buffer_1_out));
  assign controlled_buffer_1_out = in_3 ? out_6 : 8'bz;  // Controlled_Buffer controlled_buffer_2
  _1_byte_Register u_1_byte_register_2 (.o(out_7), .s(in_2), .e(in_4), .i(controlled_buffer_1_out));
  assign controlled_buffer_1_out = in_4 ? out_7 : 8'bz;  // Controlled_Buffer controlled_buffer_3
endmodule

module Stepper (
  input  reset,
  input  clk,
  output Step_1,
  output Step_2,
  output Step_3,
  output Step_4,
  output Step_5,
  output Step_6,
  output Step_7
);

  wire M1_o, M2_o, M3_o, M4_o, M5_o, M6_o, M7_o, M8_o, M9_o, M10_o, M11_o, not_1_out, not_2_out, not_3_out,
       not_4_out, not_5_out, not_6_out, not_7_out, not_8_out, or_1_out, or_2_out;

  not not_1 (not_1_out, clk);
  not not_2 (not_2_out, reset);
  or or_1 (or_1_out, reset, not_1_out);
  or or_2 (or_2_out, reset, clk);
  or or_3 (Step_1, reset, not_3_out);
  _1_bit_m M1 (.o(M1_o), .i(not_2_out), .s(or_1_out));
  not not_3 (not_3_out, M2_o);
  _1_bit_m M2 (.o(M2_o), .i(M1_o), .s(or_2_out));
  and and_1 (Step_2, M2_o, not_4_out);
  not not_4 (not_4_out, M4_o);
  _1_bit_m M3 (.o(M3_o), .i(M2_o), .s(or_1_out));
  and and_2 (Step_3, M4_o, not_5_out);
  _1_bit_m M4 (.o(M4_o), .i(M3_o), .s(or_2_out));
  not not_5 (not_5_out, M6_o);
  _1_bit_m M5 (.o(M5_o), .i(M4_o), .s(or_1_out));
  and and_3 (Step_4, M6_o, not_6_out);
  _1_bit_m M6 (.o(M6_o), .i(M5_o), .s(or_2_out));
  _1_bit_m M7 (.o(M7_o), .i(M6_o), .s(or_1_out));
  not not_6 (not_6_out, M8_o);
  _1_bit_m M8 (.o(M8_o), .i(M7_o), .s(or_2_out));
  and and_4 (Step_5, M8_o, not_7_out);
  _1_bit_m M9 (.o(M9_o), .i(M8_o), .s(or_1_out));
  not not_7 (not_7_out, M10_o);
  _1_bit_m M10 (.o(M10_o), .i(M9_o), .s(or_2_out));
  and and_5 (Step_6, M10_o, not_8_out);
  not not_8 (not_8_out, Step_7);
  _1_bit_m M11 (.o(M11_o), .i(M10_o), .s(or_1_out));
  _1_bit_m M12 (.o(Step_7), .i(M11_o), .s(or_2_out));
endmodule

module RAM_Register (
  input  [7:0] i,
  input  s,
  input  e,
  output [7:0] o
);

  wire [7:0] n1_byte_memory_1_o;

  _1_byte_Memory u_1_byte_memory_1 (.o(n1_byte_memory_1_o), .i(i), .s(s));
  Hex_Digit_Display hex_digit_display_1 (.value(n1_byte_memory_1_o[3:0]));  // open: dp
  Hex_Digit_Display hex_digit_display_2 (.value(n1_byte_memory_1_o[7:4]));  // open: dp
  _1_byte_Enabler u_1_byte_enabler_1 (.o(o), .i(n1_byte_memory_1_o), .e(e));
endmodule

module RAM_Register_Area (
  input  y,
  input  x,
  input  [7:0] bus_in,
  input  [7:0] bus_out,
  input  s,
  input  e
);

  wire and_1_out, and_2_out, X_out;

  and u_X (X_out, x, y);
  LED led_1 (.in(X_out));
  and and_1 (and_1_out, X_out, s);
  and and_2 (and_2_out, X_out, e);
  RAM_Register ram_register_1 (.o(bus_out), .i(bus_in), .s(and_1_out), .e(and_2_out));
endmodule

module RAM_256 (
  input  [7:0] in_1,
  input  in_2,
  input  in_3,
  input  in_4,
  input  [7:0] in_5,
  output [7:0] out_6
);

  wire n4x16_decoder0_1_out_5, n4x16_decoder0_1_out_6, n4x16_decoder0_1_out_7, n4x16_decoder0_1_out_8,
       n4x16_decoder0_1_out_9, n4x16_decoder0_1_out_10, n4x16_decoder0_1_out_11, n4x16_decoder0_1_out_12,
       n4x16_decoder0_1_out_13, n4x16_decoder0_1_out_14, n4x16_decoder0_1_out_15, n4x16_decoder0_1_out_16,
       n4x16_decoder0_1_out_17, n4x16_decoder0_1_out_18, n4x16_decoder0_1_out_19, n4x16_decoder0_1_out_20,
       n4x16_decoder1_1_out_5, n4x16_decoder1_1_out_6, n4x16_decoder1_1_out_7, n4x16_decoder1_1_out_8,
       n4x16_decoder1_1_out_9, n4x16_decoder1_1_out_10, n4x16_decoder1_1_out_11, n4x16_decoder1_1_out_12,
       n4x16_decoder1_1_out_13, n4x16_decoder1_1_out_14, n4x16_decoder1_1_out_15, n4x16_decoder1_1_out_16,
       n4x16_decoder1_1_out_17, n4x16_decoder1_1_out_18, n4x16_decoder1_1_out_19, n4x16_decoder1_1_out_20,
       undriven, undriven_2, undriven_5, undriven_6, undriven_9, undriven_10;
  wire [7:0] n1_byte_memory_1_o, undriven_3, undriven_4, undriven_7, undriven_8, undriven_11, undriven_12;

  _1_byte_Memory u_1_byte_memory_1 (.o(n1_byte_memory_1_o), .i(in_1), .s(in_2));
  _4x16_Decoder0 u_4x16_decoder0_1 (
    .out_20(n4x16_decoder0_1_out_20), .out_5(n4x16_decoder0_1_out_5), .out_6(n4x16_decoder0_1_out_6),
    .out_7(n4x16_decoder0_1_out_7), .out_8(n4x16_decoder0_1_out_8), .out_9(n4x16_decoder0_1_out_9),
    .out_10(n4x16_decoder0_1_out_10), .out_11(n4x16_decoder0_1_out_11), .out_12(n4x16_decoder0_1_out_12),
    .out_13(n4x16_decoder0_1_out_13), .out_14(n4x16_decoder0_1_out_14), .out_15(n4x16_decoder0_1_out_15),
    .out_16(n4x16_decoder0_1_out_16), .out_17(n4x16_decoder0_1_out_17), .out_18(n4x16_decoder0_1_out_18),
    .out_19(n4x16_decoder0_1_out_19), .d(n1_byte_memory_1_o[4]), .a(n1_byte_memory_1_o[7]),
    .b(n1_byte_memory_1_o[6]), .c(n1_byte_memory_1_o[5]));
  _4x16_Decoder1 u_4x16_decoder1_1 (
    .out_20(n4x16_decoder1_1_out_20), .out_5(n4x16_decoder1_1_out_5), .out_6(n4x16_decoder1_1_out_6),
    .out_7(n4x16_decoder1_1_out_7), .out_8(n4x16_decoder1_1_out_8), .out_9(n4x16_decoder1_1_out_9),
    .out_10(n4x16_decoder1_1_out_10), .out_11(n4x16_decoder1_1_out_11), .out_12(n4x16_decoder1_1_out_12),
    .out_13(n4x16_decoder1_1_out_13), .out_14(n4x16_decoder1_1_out_14), .out_15(n4x16_decoder1_1_out_15),
    .out_16(n4x16_decoder1_1_out_16), .out_17(n4x16_decoder1_1_out_17), .out_18(n4x16_decoder1_1_out_18),
    .out_19(n4x16_decoder1_1_out_19), .d(n1_byte_memory_1_o[0]), .a(n1_byte_memory_1_o[3]),
    .b(n1_byte_memory_1_o[2]), .c(n1_byte_memory_1_o[1]));
  RAM_Register_Area ram_register_area_1 (
    .x(n4x16_decoder0_1_out_5), .bus_in(in_5), .bus_out(out_6), .s(in_3), .e(in_4), .y(n4x16_decoder1_1_out_5));
  RAM_Register_Area ram_register_area_2 (
    .x(n4x16_decoder0_1_out_6), .bus_in(in_5), .bus_out(out_6), .s(in_3), .e(in_4), .y(n4x16_decoder1_1_out_5));
  RAM_Register_Area ram_register_area_3 (
    .x(n4x16_decoder0_1_out_5), .bus_in(undriven_3), .bus_out(undriven_4), .s(undriven), .e(undriven_2),
    .y(n4x16_decoder1_1_out_6));
  RAM_Register_Area ram_register_area_4 (
    .x(n4x16_decoder0_1_out_5), .bus_in(undriven_7), .bus_out(undriven_8), .s(undriven_5), .e(undriven_6),
    .y(n4x16_decoder1_1_out_7));
  RAM_Register_Area ram_register_area_5 (
    .x(n4x16_decoder0_1_out_5), .bus_in(undriven_11), .bus_out(undriven_12), .s(undriven_9), .e(undriven_10),
    .y(n4x16_decoder1_1_out_8));
endmodule

module Register (
  input  [7:0] i,
  input  s,
  input  e,
  output [7:0] o
);

  wire [7:0] n1_byte_memory_1_o;

  _1_byte_Memory u_1_byte_memory_1 (.o(n1_byte_memory_1_o), .i(i), .s(s));
  _1_byte_Enabler u_1_byte_enabler_1 (.o(i), .i(n1_byte_memory_1_o), .e(e));

  assign o = i;
endmodule
